# Fritzing sketch driveboard (saved by Fritzing 0.9.2b)
circuit board: 19.05cm x 17.78cm

parts:
  XTAL1 = Crystal [frequency="16 Mhz" package=THT]
  Atmega328P = atmega168 [package=dip]
  R1 = Resistor [tolerance=±5% resistance=10k package=THT]
  R2 = Resistor [tolerance=±5% resistance=10k package=THT]
  R3 = Resistor [tolerance=±5% resistance=10k package=THT]
  R9 = Resistor [tolerance=±5% resistance=10k package=THT]
  R8 = Resistor [tolerance=±5% resistance=10k package=THT]
  R7 = Resistor [tolerance=±5% resistance=10k package=THT]
  R5 = Resistor [tolerance=±5% resistance=10k package=THT]
  R6 = Resistor [tolerance=±5% resistance=10k package=THT]
  R4 = Resistor [tolerance=±5% resistance=10k package=THT]
  C2 = Ceramic Capacitor [capacitance=22pF package="100 mil [THT, multilayer]"]
  C1 = Ceramic Capacitor [capacitance=22pF package="100 mil [THT, multilayer]"]
  SSR_AC3 = female pin header, 1 pin [form="♀ (female)"]
  SSR_AC4 = female pin header, 1 pin [form="♀ (female)"]
  SSR_DC+ = female pin header, 1 pin [form="♀ (female)"]
  SSR_DC- = female pin header, 1 pin [form="♀ (female)"]
  D1 = Rectifier Diode [part_number=1N4004 package="300 mil [THT]"]
  D2 = Rectifier Diode [part_number=1N4004 package="300 mil [THT]"]
  R10 = Resistor [tolerance=±5% resistance=360 package=THT]
  R11 = Resistor [tolerance=±5% resistance=360 package=THT]
  R12 = Resistor [tolerance=±5% resistance=6.5k package=THT]
  R13 = Resistor [tolerance=±5% resistance=10k package=THT]
  R14 = Resistor [tolerance=±1% resistance=6.49k package=THT]
  R15 = Resistor [tolerance=±1% resistance=11.5k package=THT]
  R16 = Resistor [tolerance=±1% resistance=11.5k package=THT]
  G2 = female pin header, 1 pin [form="♀ (female)"]
  G1 = female pin header, 1 pin [form="♀ (female)"]
  G4 = female pin header, 1 pin [form="♀ (female)"]
  G3 = female pin header, 1 pin [form="♀ (female)"]
  G6 = female pin header, 1 pin [form="♀ (female)"]
  G5 = female pin header, 1 pin [form="♀ (female)"]
  G8 = female pin header, 1 pin [form="♀ (female)"]
  G7 = female pin header, 1 pin [form="♀ (female)"]
  G10 = female pin header, 1 pin [form="♀ (female)"]
  G9 = female pin header, 1 pin [form="♀ (female)"]
  G12 = female pin header, 1 pin [form="♀ (female)"]
  G11 = female pin header, 1 pin [form="♀ (female)"]
  G13 = female pin header, 1 pin [form="♀ (female)"]
  G14 = female pin header, 1 pin [form="♀ (female)"]
  G15 = female pin header, 1 pin [form="♀ (female)"]
  G16 = female pin header, 1 pin [form="♀ (female)"]
  G17 = female pin header, 1 pin [form="♀ (female)"]
  G18 = female pin header, 1 pin [form="♀ (female)"]
  G19 = female pin header, 1 pin [form="♀ (female)"]
  G20 = female pin header, 1 pin [form="♀ (female)"]
  G21 = female pin header, 1 pin [form="♀ (female)"]
  G22 = female pin header, 1 pin [form="♀ (female)"]
  G23 = female pin header, 1 pin [form="♀ (female)"]
  G24 = female pin header, 1 pin [form="♀ (female)"]
  G25 = female pin header, 1 pin [form="♀ (female)"]
  G26 = female pin header, 1 pin [form="♀ (female)"]
  J1 = female pin header, 6 pins [form="♀ (female)"]
  J2 = female pin header, 4 pins [form="♀ (female)"]
  J3 = female pin header, 6 pins [form="♀ (female)"]
  J4 = female pin header, 4 pins [form="♀ (female)"]
  J5 = female pin header, 6 pins [form="♀ (female)"]
  J6 = female pin header, 4 pins [form="♀ (female)"]
  RaspberryPi_(optional) = double row female pin header, 26 pins [form="♀ (female)"]
  gecko_sense = Resistor [tolerance=±5% resistance=10k package=THT]
  SMC11_sense_(optional) = Resistor [tolerance=±5% resistance=10k package=THT]
  G27 = female pin header, 1 pin [form="♀ (female)"]
  G28 = female pin header, 1 pin [form="♀ (female)"]
  G29 = female pin header, 1 pin [form="♀ (female)"]  # not connected
  G30 = female pin header, 1 pin [form="♀ (female)"]  # not connected
  C4 = Ceramic Capacitor [capacitance=100nF voltage=50V package="100 mil [THT, multilayer]"]
  C5 = Ceramic Capacitor [capacitance=100nF voltage=50V package="100 mil [THT, multilayer]"]
  C6 = Ceramic Capacitor [capacitance=100nF voltage=50V package="100 mil [THT, multilayer]"]
  C7 = Ceramic Capacitor [capacitance=100nF voltage=50V package="100 mil [THT, multilayer]"]
  C9 = Ceramic Capacitor [capacitance=100nF package="100 mil [THT, multilayer]"]
  C10 = Ceramic Capacitor [capacitance=100nF package="100 mil [THT, multilayer]"]
  C11 = Ceramic Capacitor [capacitance=100nF voltage=50V package="100 mil [THT, multilayer]"]
  R17 = Resistor [tolerance=±5% resistance=360 package=THT]
  z1 = RJ45 Jack [package=rj45-8]
  z2 = RJ45 Jack [package=rj45-8]
  chiller = RJ45 Jack [package=rj45-8]
  laser = RJ45 Jack [package=rj45-8]
  door2 = RJ45 Jack [package=rj45-8]
  door1 = RJ45 Jack [package=rj45-8]
  y2 = RJ45 Jack [package=rj45-8]
  y1 = RJ45 Jack [package=rj45-8]
  x2 = RJ45 Jack [package=rj45-8]
  x1 = RJ45 Jack [package=rj45-8]
  stepper_z = RJ45 Jack [package=rj45-8]
  stepper_y = RJ45 Jack [package=rj45-8]
  stepper_x = RJ45 Jack [package=rj45-8]
  e-stop = RJ45 Jack [package=rj45-8]
  assists = RJ45 Jack [package=rj45-8]
  AC_IN1 = screw terminal, 5 pins
  AC_IN2 = screw terminal, 5 pins
  GND_IN = screw terminal, 6 pins
  5V = screw terminal, 2 pins
  24V = screw terminal, 6 pins
  C3 = Electrolytic Capacitor [capacitance=1mF voltage=50V package="300 mil [THT, electrolytic]"]
  C12 = Electrolytic Capacitor [capacitance=47µF voltage=50V package="100 mil [THT, electrolytic]"]
  NAND = IC, DIP package, 14 pins [chip_label=NAND part_number=CD74HCT10E]
  AND = IC, DIP package, 14 pins [chip_label=AND part_number=CD74HCT11E]
  air_relay = IC, DIP package, 4 pins [chip_label=SSR part_number=AQY212GH]
  aux1_relay = IC, DIP package, 4 pins [chip_label=SSR part_number=AQY212GH]
  stepperterm1 = screw terminal, 4 pins
  stepperterm2 = screw terminal, 4 pins
  stepperterm3 = screw terminal, 4 pins
  auto_reset = male pin header, 2 pins [form="♂ (male)"]
  jmp1 = male pin header, 2 pins [form="♂ (male)"]
  jmp2 = male pin header, 2 pins [form="♂ (male)"]
  D5 = male pin header, 2 pins [form="♂ (male)"]
  Gecko_(G203V/G201X)_X-axis = male pin header, 12 pins [form="♂ (male)"]
  Gecko_(G203V/G201X)_Y-axis = male pin header, 12 pins [form="♂ (male)"]
  Gecko_(G203V/G201X)_Z-axis = male pin header, 12 pins [form="♂ (male)"]
  power5V = male pin header, 2 pins [form="♂ (male)"]
  P9 = double row male pin header, 44 pins [form="♂ (male)"]
  P8 = double row male pin header, 44 pins [form="♂ (male)"]
  extension = male pin header, 6 pins [form="♂ (male)"]
  serial = male pin header, 4 pins [form="♂ (male)"]
  ICSP = double row male pin header, 6 pins [form="♂ (male)"]
  e-stop_relay = IC, DIP package, 6 pins [chip_label=SSR part_number=AQV252G]

nets:
  N1: XTAL1.pin_0, Atmega328P.XLAT1, C2.0
  N2: XTAL1.pin_1, Atmega328P.XLAT2, C1.0
  RESET: Atmega328P.RESET, RaspberryPi_(optional).pin25, auto_reset.pin1, auto_reset.pin2, P8.pin21, ICSP.pin3
  RX: Atmega328P.D0_(RX), RaspberryPi_(optional).pin4, P9.pin11, serial.pin4
  TX: Atmega328P.D1_(TX), R12.Pin_1
  SENSOR:DOOR: Atmega328P.D2, NAND.pin5, AND.pin8
  SENSOR:CHILLER: Atmega328P.D3_(PWM), R7.Pin_0, chiller.2, chiller.4, chiller.5, chiller.6, NAND.pin10
  RELAY:AIR: Atmega328P.D4, R10.Pin_0
  5V: Atmega328P.VCC, Atmega328P.AVCC, SSR_DC+.pin1, RaspberryPi_(optional).pin1, C4.1, C6.0, C7.0, C9.0, C10.0, C11.1, R17.Pin_0, z1.1, z1.3, z2.1, z2.3, chiller.1, chiller.3, laser.1, laser.3, door2.1, door2.3, door1.1, door1.3, y2.1, y2.3, y1.1, y1.3, x2.1, x2.3, x1.1, x1.3, 5V.pin2, C3.+, C12.+, NAND.pin1, NAND.pin9, NAND.pin13, NAND.pin14, AND.pin9, AND.pin14, power5V.pin2, P9.pin2, P9.pin43, extension.pin1, serial.pin1, ICSP.pin6
  GND: Atmega328P.GND, R1.Pin_1, R2.Pin_1, R3.Pin_1, R9.Pin_1, R8.Pin_1, R7.Pin_1, R5.Pin_1, R6.Pin_1, R4.Pin_1, C2.1, C1.1, SSR_DC-.pin1, R13.Pin_0, G2.pin1, G1.pin1, G4.pin1, G3.pin1, G6.pin1, G5.pin1, G8.pin1, G7.pin1, G10.pin1, G9.pin1, G12.pin1, G11.pin1, G13.pin1, G14.pin1, G15.pin1, G16.pin1, G17.pin1, G18.pin1, G19.pin1, G20.pin1, G21.pin1, G22.pin1, G23.pin1, G24.pin1, G25.pin1, G26.pin1, RaspberryPi_(optional).pin3, gecko_sense.Pin_0, C6.1, C7.1, C9.1, C10.1, C11.0, z1.7, z1.8, z2.7, z2.8, chiller.7, chiller.8, laser.7, laser.8, door2.7, door2.8, door1.7, door1.8, y2.7, y2.8, y1.7, y1.8, x2.7, x2.8, x1.7, x1.8, C3.-, C12.-, NAND.pin7, AND.pin7, air_relay.pin2, aux1_relay.pin2, jmp2.pin1, D5.pin2, Gecko_(G203V/G201X)_X-axis.pin3, Gecko_(G203V/G201X)_Y-axis.pin3, Gecko_(G203V/G201X)_Z-axis.pin3, power5V.pin1, P9.pin21, P9.pin22, P9.pin23, P9.pin24, extension.pin2, serial.pin2, ICSP.pin4, e-stop_relay.pin4, e-stop_relay.pin6
  LASER:AUX2: Atmega328P.D5_(PWM), laser.5, D5.pin1
  LASER:PWM: Atmega328P.D6_(PWM), laser.4
  RELAY:AUX1: Atmega328P.D7, R11.Pin_1
  STEP:X: Atmega328P.D8, J1.pin4, Gecko_(G203V/G201X)_X-axis.pin4
  STEP:Y: Atmega328P.D9_(PWM), J3.pin4, Gecko_(G203V/G201X)_Y-axis.pin4
  STEP:Z: Atmega328P.D10_(PWM), J5.pin4, Gecko_(G203V/G201X)_Z-axis.pin4
  DIR:X/PB3: Atmega328P.D11_(PWM), J1.pin3, Gecko_(G203V/G201X)_X-axis.pin5, ICSP.pin5
  DIR:Y/PB4: Atmega328P.D12, J3.pin3, Gecko_(G203V/G201X)_Y-axis.pin5, ICSP.pin1
  DIR:Z/PB5: Atmega328P.D13, J5.pin3, Gecko_(G203V/G201X)_Z-axis.pin5, ICSP.pin2
  LIMIT:X1: Atmega328P.A0, R1.Pin_0, x1.2, x1.4, x1.5, x1.6, AND.pin5
  LIMIT:X2: Atmega328P.A1, R2.Pin_0, x2.2, x2.4, x2.5, x2.6, AND.pin4
  LIMIT:Y1: Atmega328P.A2, R3.Pin_0, y1.2, y1.4, y1.5, y1.6, AND.pin3
  LIMIT:Y2: Atmega328P.A3, R4.Pin_0, y2.2, y2.4, y2.5, y2.6, AND.pin2
  LIMIT:Z1: Atmega328P.A4, R5.Pin_0, z1.2, z1.4, z1.5, z1.6, AND.pin1
  LIMIT:Z2: Atmega328P.A5, R6.Pin_0, z2.2, z2.4, z2.5, z2.6, AND.pin13
  SENSOR:DOOR1: R9.Pin_0, door1.2, door1.4, door1.5, door1.6, AND.pin10
  SENSOR:DOOR2: R8.Pin_0, door2.2, door2.4, door2.5, door2.6, AND.pin11
  AC:24V2/AC:LASER2: SSR_AC3.pin1, AC_IN2.pin1, AC_IN2.pin2
  AC:5V2/AC:EXTRA2/AC:IN2: SSR_AC4.pin1, AC_IN2.pin3, AC_IN2.pin4, AC_IN2.pin5
  ASSIST:AIR+: D1.cathode, assists.1, assists.3, 24V.pin4, air_relay.pin4
  24V-/ASSIST:AIR-/ASSIST:AUX2-: D1.anode, D2.anode, J1.pin2, J1.pin5, J1.pin6, J3.pin2, J3.pin5, J3.pin6, J5.pin2, J5.pin5, J5.pin6, C5.0, assists.2, assists.4, assists.6, assists.8, 24V.pin1, 24V.pin3, 24V.pin5, Gecko_(G203V/G201X)_X-axis.pin12, Gecko_(G203V/G201X)_Y-axis.pin12, Gecko_(G203V/G201X)_Z-axis.pin12
  ASSIST:AUX2+: D2.cathode, assists.5, assists.7, 24V.pin2, aux1_relay.pin4
  N3: R10.Pin_1, air_relay.pin1
  N4: R11.Pin_0, aux1_relay.pin1
  TX:3V3: R12.Pin_0, R13.Pin_1, RaspberryPi_(optional).pin5, P9.pin12, serial.pin3
  N5: R14.Pin_0, Gecko_(G203V/G201X)_X-axis.pin2
  N6: R14.Pin_1, Gecko_(G203V/G201X)_X-axis.pin1
  N7: R15.Pin_0, Gecko_(G203V/G201X)_Y-axis.pin2
  N8: R15.Pin_1, Gecko_(G203V/G201X)_Y-axis.pin1
  N9: R16.Pin_0, Gecko_(G203V/G201X)_Z-axis.pin2
  N10: R16.Pin_1, Gecko_(G203V/G201X)_Z-axis.pin1
  24V: J1.pin1, J3.pin1, J5.pin1, C5.1, 24V.pin6, air_relay.pin3, aux1_relay.pin3, Gecko_(G203V/G201X)_X-axis.pin11, Gecko_(G203V/G201X)_Y-axis.pin11, Gecko_(G203V/G201X)_Z-axis.pin11
  STPX:A: J2.pin1, stepper_x.1, stepper_x.3, stepperterm1.pin4, Gecko_(G203V/G201X)_X-axis.pin10
  STPX:A': J2.pin2, stepper_x.2, stepper_x.6, stepperterm1.pin3, Gecko_(G203V/G201X)_X-axis.pin9
  STPX:B: J2.pin3, stepper_x.4, stepper_x.8, stepperterm1.pin2, Gecko_(G203V/G201X)_X-axis.pin8
  STPX:B': J2.pin4, stepper_x.5, stepper_x.7, stepperterm1.pin1, Gecko_(G203V/G201X)_X-axis.pin7
  STPY:A: J4.pin1, stepper_y.1, stepper_y.3, stepperterm2.pin4, Gecko_(G203V/G201X)_Y-axis.pin10
  STPY:A': J4.pin2, stepper_y.2, stepper_y.6, stepperterm2.pin3, Gecko_(G203V/G201X)_Y-axis.pin9
  STPY:B: J4.pin3, stepper_y.4, stepper_y.8, stepperterm2.pin2, Gecko_(G203V/G201X)_Y-axis.pin8
  STPY:B': J4.pin4, stepper_y.5, stepper_y.7, stepperterm2.pin1, Gecko_(G203V/G201X)_Y-axis.pin7
  STPZ:A: J6.pin1, stepper_z.1, stepper_z.3, stepperterm3.pin4, Gecko_(G203V/G201X)_Z-axis.pin10
  STPZ:A': J6.pin2, stepper_z.2, stepper_z.6, stepperterm3.pin3, Gecko_(G203V/G201X)_Z-axis.pin9
  STPZ:B: J6.pin3, stepper_z.4, stepper_z.8, stepperterm3.pin2, Gecko_(G203V/G201X)_Z-axis.pin8
  STPZ:B': J6.pin4, stepper_z.5, stepper_z.7, stepperterm3.pin1, Gecko_(G203V/G201X)_Z-axis.pin7
  RSENSE: RaspberryPi_(optional).pin13, gecko_sense.Pin_1, SMC11_sense_(optional).Pin_0, P8.pin26
  BBGPIO2:10/RPGPIO:17: RaspberryPi_(optional).pin21, P8.pin25, extension.pin5
  BBGPIO2:8/RPGPIO:4: RaspberryPi_(optional).pin23, P8.pin24, extension.pin4
  BBGPIO2:6/RPGPIO:3: RaspberryPi_(optional).pin24, P8.pin23, extension.pin3
  3V3: RaspberryPi_(optional).pin26, SMC11_sense_(optional).Pin_1, P9.pin1, extension.pin6
  5V-: G27.pin1, G28.pin1, C4.0, e-stop.2, e-stop.4, e-stop.5, e-stop.6, e-stop.7, e-stop.8, 5V.pin1, jmp1.pin2, e-stop_relay.pin5
  N11: R17.Pin_1, e-stop_relay.pin1
  LASER:DIS: laser.2, laser.6, NAND.pin8
  N12: e-stop.1, e-stop.3, jmp1.pin1, jmp2.pin2, e-stop_relay.pin2
  AC:24V1/AC:5V1/AC:EXTRA1/AC:IN1/AC:LASER1: AC_IN1.pin1, AC_IN1.pin2, AC_IN1.pin3, AC_IN1.pin4, AC_IN1.pin5
  GND:24V/GND:5V/GND:EXTRA/GND:FRAME/GND:IN/GND:LASER: GND_IN.pin1, GND_IN.pin2, GND_IN.pin3, GND_IN.pin4, GND_IN.pin5, GND_IN.pin6
  N13: NAND.pin2, NAND.pin6
  N14: NAND.pin3, AND.pin12
  N15: NAND.pin4, AND.pin6
  N16: NAND.pin11, NAND.pin12

notes:
  Lasersaur
  AC_in_2
  AC_laser_psu_1
  AC_in_1
  AC_5V_psu_1
  AC_extra_1
  AC_extra_2
  (12A max)
  AC_24V_psu_1
  AC_laser_psu_2
  AC_5V_psu_2
  AC_24V_psu_2
  GND_in
  DC_in_5V-
  aux1_assist+
  GND_laser_psu
  (AC total ->12A max)
  (5A max)
  GND_24V_psu
  DC_in_5V+
  (10A max)
  GND_5V_psu
  aux1_assist-
  GND_extra
  air_assist-
  air_assist+
  GND_frame
  DriveBoard  v14.03
  DC_in_24V-
  DC_in_24V+
  3
  4
  46
  45
  TX
  RX (UART1)
  5V (VDD)
  gnd
  PB1
  PB5
  PB0
  PD7
  PD5
  PD4
  PD2
  RX
  PC5
  PC0
  VCC
  IN1
  OUT1
  OUT3
  IN3
  IN2
  OUT2
  GND
  voltage_divider
  A
  A'
  B
  B'
  grn<->wgrn
  BeagleBone
  24V
  dis
  dir
  step
  current_set
  11.5k
  360
  first four pins do not connect
  10k
  6.49k
  (optional)
  (screw terminals -> 5A max)
  1
  pwm:blu, dis:grn, gnd:brn
  cable mapping -> A:wgr/wor, A':gr/or, B:bl/wbl, B':br/wbr
  *
  1000uF
  22pF
  -----------
  aux2:wbl
  align pins here at this side
  Nanotec SMC11 (optional) X-axis
  Nanotec SMC11 (optional) Y-axis
  Nanotec SMC11 (optional) Z-axis
  (modular jacks -> 3A max)
  (1A max)
  MC74AC11NG
  MC74AC10NG
  GPIO_2
  GPIO_3
  GPIO_4
  GPIO_17
  GPIO2_12
  GPIO2_7
  GPIO2_22
  GPIO_7
  R = 47*I/(7–I)*1000
  5V
  GPIO2_6
  GPIO2_8
  GPIO2_10
  3.3V
  (e-stop interlock to be closed for operation)
  100nF
  47uF
  BeagleBone Black
  DriveBoard v14.03
  +
  -
  PF240D25
